// Logisim project SynthBite16.circ as structural Verilog: 1 circuit, main circuit SynthBite16
module SynthBite16 (
  input  in_1,
  input  [15:0] in_2,
  input  [15:0] in_3,
  input  in_4,
  input  in_5,
  input  in_6,
  input  in_7,
  input  in_8
);

  wire AC_p2, AC_p3, AC_p18, AC_p19, AC_p20, AC_p21, AC_p22, AC_p23, AC_p24, AC_p25, AC_p26, AC_p27, AC_p28,
       adder_1_cout, adder_2_cout, and_4_out, and_5_out, and_6_out, and_7_out, button_1_out, button_2_out,
       carry_q, comparator_1_eq, comparator_1_gt, comparator_1_lt, controlled_buffer_1_out,
       controlled_buffer_2_out, controlled_buffer_3_out, controlled_buffer_4_out, controlled_buffer_5_out,
       controlled_buffer_6_out, controlled_buffer_7_out, controlled_buffer_8_out, controlled_buffer_9_out,
       controlled_buffer_10_out, controlled_buffer_11_out, controlled_buffer_12_out,
       controlled_buffer_13_out, controlled_buffer_14_out, controlled_buffer_15_out,
       controlled_buffer_16_out, decoder_1_out0, decoder_1_out1, decoder_1_out2, decoder_1_out3,
       decoder_1_out5, decoder_1_out10, decoder_1_out11, decoder_1_out12, decoder_1_out13, decoder_2_out0,
       decoder_2_out1, decoder_2_out3, decoder_2_out5, decoder_2_out10, decoder_2_out11, decoder_2_out12,
       decoder_2_out13, decoder_2_out14, decoder_2_out15, demultiplexer_1_out0, demultiplexer_1_out1,
       demultiplexer_1_out2, demultiplexer_1_out3, demultiplexer_1_out4, demultiplexer_1_out5,
       demultiplexer_1_out6, demultiplexer_1_out7, mAC_p2, MasterClock_out, multiplexer_5_out, nand_1_out,
       not_3_out, or_2_out, or_3_out, or_4_out, or_6_out, PC_carry, register_10_q, SP_carry,
       subtractor_1_bout, undriven, undriven_2, undriven_3, undriven_5, undriven_6, undriven_8, undriven_9,
       undriven_10;
  wire [0:0] DR_q, not_2_out;
  wire [2:0] SP_q;
  wire [3:0] CWR_q;
  wire [6:0] register_9_q_2;
  wire [9:0] counter_1_q;
  wire [9:9] IR_q_2;
  wire [11:0] AR_q, controlled_buffer_17_out, PC_q;
  wire [15:0] adder_1_out, adder_2_out, adder_3_out, and_1_out, and_2_out, and_3_out,
       controlled_buffer_18_out, dAC_p18, DR_q_2, mAC_p1, multiplexer_1_out, multiplexer_2_out,
       multiplexer_3_out, multiplexer_4_out, not_1_out, or_1_out, rand_q, register_1_q, register_2_q,
       register_3_q, register_4_q, register_5_q, register_6_q, register_7_q, register_8_q, subtractor_1_out,
       subtractor_2_out, undriven_7, xor_1_out, xor_2_out;
  wire [15:1] IR_q;
  wire [15:7] register_9_q;
  wire [15:15] undriven_4;
  wire [31:0] CNTRL_MEM_data, CWR_q_2;

  Controlled_Buffer controlled_buffer_1 (.out(controlled_buffer_1_out), .en(undriven));  // open: in
  Controlled_Buffer controlled_buffer_2 (.out(controlled_buffer_2_out), .en(undriven));  // open: in
  Controlled_Buffer controlled_buffer_3 (.out(controlled_buffer_3_out), .en(undriven));  // open: in
  Controlled_Buffer controlled_buffer_4 (.out(controlled_buffer_4_out), .en(undriven));  // open: in
  Controlled_Buffer controlled_buffer_5 (.out(controlled_buffer_5_out), .en(undriven));  // open: in
  Controlled_Buffer controlled_buffer_6 (.out(controlled_buffer_6_out), .en(undriven));  // open: in
  Controlled_Buffer controlled_buffer_7 (.out(controlled_buffer_7_out), .en(undriven));  // open: in
  Controlled_Buffer controlled_buffer_8 (.out(controlled_buffer_8_out), .en(undriven));  // open: in
  Controlled_Buffer controlled_buffer_9 (.out(controlled_buffer_9_out), .en(undriven));  // open: in
  Controlled_Buffer controlled_buffer_10 (.out(controlled_buffer_10_out), .en(undriven));  // open: in
  Controlled_Buffer controlled_buffer_11 (.out(controlled_buffer_11_out), .en(undriven));  // open: in
  Controlled_Buffer controlled_buffer_12 (.out(controlled_buffer_12_out), .en(undriven));  // open: in
  Controlled_Buffer controlled_buffer_13 (.out(controlled_buffer_13_out), .en(undriven));  // open: in
  Controlled_Buffer controlled_buffer_14 (.out(controlled_buffer_14_out), .en(undriven));  // open: in
  Controlled_Buffer controlled_buffer_15 (.out(controlled_buffer_15_out), .en(undriven));  // open: in
  Controlled_Buffer controlled_buffer_16 (.out(controlled_buffer_16_out), .en(undriven));  // open: in
  Clock MasterClock (.out(MasterClock_out));
  LED led_1 (.in(MasterClock_out));
  Counter #(.max('h7), .width(3)) SP (
    .clr(button_1_out), .up(CWR_q_2[22]), .count(CWR_q_2[21]), .clk(MasterClock_out), .carry(SP_carry),
    .Q(SP_q));  // open: load, D
  assign controlled_buffer_17_out = decoder_1_out5 ? AR_q : 12'bz;  // Controlled_Buffer controlled_buffer_17
  assign {{4{controlled_buffer_18_out[15]}}, controlled_buffer_18_out[11:0]} = decoder_1_out13 ? {IR_q, IR_q_2[9]} : 16'bz;  // Controlled_Buffer controlled_buffer_18
  assign {{4{controlled_buffer_18_out[15]}}, controlled_buffer_18_out[11:0]} = decoder_1_out12 ? multiplexer_1_out : 16'bz;  // Controlled_Buffer controlled_buffer_19
  Multiplexer #(.select(3), .width(16)) multiplexer_1 (
    .in0(register_1_q), .in1(register_2_q), .in2(register_3_q), .in3(register_4_q), .in4(register_5_q),
    .in5(register_6_q), .in6(register_7_q), .in7(register_8_q), .out(multiplexer_1_out), .sel(SP_q));
  Register #(.width(12)) AR (.D(IR_q[15:4]), .en(decoder_2_out5), .clk(MasterClock_out), .Q(AR_q), .clr(button_1_out));
  Register #(.trigger("falling"), .width(16)) DR (
    .D({{4{controlled_buffer_18_out[15]}}, controlled_buffer_18_out[11:0]}), .en(decoder_2_out10),
    .clk(MasterClock_out), .Q({DR_q_2[14:0], DR_q[0]}), .clr(button_1_out));
  Counter #(.max('hfff), .width(12)) PC (
    .clr(button_1_out), .load(decoder_2_out3), .up(1'b1), .count(undriven_2), .clk(MasterClock_out),
    .D(IR_q[15:4]), .carry(PC_carry), .Q(PC_q));
  LED led_2 (.in(SP_carry));
  Demultiplexer #(.enable("true"), .select(3)) demultiplexer_1 (
    .out0(demultiplexer_1_out0), .out1(demultiplexer_1_out1), .out2(demultiplexer_1_out2),
    .out3(demultiplexer_1_out3), .out4(demultiplexer_1_out4), .out5(demultiplexer_1_out5),
    .out6(demultiplexer_1_out6), .out7(demultiplexer_1_out7), .in(1'b1), .sel(SP_q), .en(decoder_2_out15));
  Register #(.width(16)) register_1 (
    .D({{4{controlled_buffer_18_out[15]}}, controlled_buffer_18_out[11:0]}), .en(demultiplexer_1_out0),
    .clk(MasterClock_out), .Q(register_1_q), .clr(button_1_out));
  Register #(.width(16)) register_2 (
    .D({{4{controlled_buffer_18_out[15]}}, controlled_buffer_18_out[11:0]}), .en(demultiplexer_1_out1),
    .clk(MasterClock_out), .Q(register_2_q), .clr(button_1_out));
  Register #(.width(16)) register_3 (
    .D({{4{controlled_buffer_18_out[15]}}, controlled_buffer_18_out[11:0]}), .en(demultiplexer_1_out2),
    .clk(MasterClock_out), .Q(register_3_q), .clr(button_1_out));
  Register #(.width(16)) register_4 (
    .D({{4{controlled_buffer_18_out[15]}}, controlled_buffer_18_out[11:0]}), .en(demultiplexer_1_out3),
    .clk(MasterClock_out), .Q(register_4_q), .clr(button_1_out));
  DotMatrix #(.matrixcols(16), .matrixrows(1)) dotmatrix_1 (
    .col0(controlled_buffer_18_out[15]), .col1(controlled_buffer_18_out[15]),
    .col2(controlled_buffer_18_out[15]), .col3(controlled_buffer_18_out[15]),
    .col4(controlled_buffer_18_out[11]), .col5(controlled_buffer_18_out[10]),
    .col6(controlled_buffer_18_out[9]), .col7(controlled_buffer_18_out[8]),
    .col8(controlled_buffer_18_out[7]), .col9(controlled_buffer_18_out[6]),
    .col10(controlled_buffer_18_out[5]), .col11(controlled_buffer_18_out[4]),
    .col12(controlled_buffer_18_out[3]), .col13(controlled_buffer_18_out[2]),
    .col14(controlled_buffer_18_out[1]), .col15(controlled_buffer_18_out[0]));
  LED led_3 (.in(PC_carry));
  Controlled_Buffer #(.width(12)) controlled_buffer_20 (.in(PC_q), .out(controlled_buffer_17_out));  // open: en
  Register #(.width(16)) register_5 (
    .D({{4{controlled_buffer_18_out[15]}}, controlled_buffer_18_out[11:0]}), .en(demultiplexer_1_out4),
    .clk(MasterClock_out), .Q(register_5_q), .clr(button_1_out));
  Register #(.width(16)) register_6 (
    .D({{4{controlled_buffer_18_out[15]}}, controlled_buffer_18_out[11:0]}), .en(demultiplexer_1_out5),
    .clk(MasterClock_out), .Q(register_6_q), .clr(button_1_out));
  Register #(.width(16)) register_7 (
    .D({{4{controlled_buffer_18_out[15]}}, controlled_buffer_18_out[11:0]}), .en(demultiplexer_1_out6),
    .clk(MasterClock_out), .Q(register_7_q), .clr(button_1_out));
  Register #(.width(16)) register_8 (
    .D({{4{controlled_buffer_18_out[15]}}, controlled_buffer_18_out[11:0]}), .en(demultiplexer_1_out7),
    .clk(MasterClock_out), .Q(register_8_q), .clr(button_1_out));
  assign controlled_buffer_18_out[0] = decoder_1_out3 ? controlled_buffer_17_out[0] : 1'bz;  // Controlled_Buffer controlled_buffer_21
  assign controlled_buffer_18_out[1] = decoder_1_out3 ? controlled_buffer_17_out[1] : 1'bz;  // Controlled_Buffer controlled_buffer_22
  assign controlled_buffer_18_out[2] = decoder_1_out3 ? controlled_buffer_17_out[2] : 1'bz;  // Controlled_Buffer controlled_buffer_23
  assign controlled_buffer_18_out[3] = decoder_1_out3 ? controlled_buffer_17_out[3] : 1'bz;  // Controlled_Buffer controlled_buffer_24
  assign controlled_buffer_18_out[4] = decoder_1_out3 ? controlled_buffer_17_out[4] : 1'bz;  // Controlled_Buffer controlled_buffer_25
  assign controlled_buffer_18_out[5] = decoder_1_out3 ? controlled_buffer_17_out[5] : 1'bz;  // Controlled_Buffer controlled_buffer_26
  assign controlled_buffer_18_out[6] = decoder_1_out3 ? controlled_buffer_17_out[6] : 1'bz;  // Controlled_Buffer controlled_buffer_27
  assign controlled_buffer_18_out[7] = decoder_1_out3 ? controlled_buffer_17_out[7] : 1'bz;  // Controlled_Buffer controlled_buffer_28
  assign controlled_buffer_18_out[8] = decoder_1_out3 ? controlled_buffer_17_out[8] : 1'bz;  // Controlled_Buffer controlled_buffer_29
  assign controlled_buffer_18_out[9] = decoder_1_out3 ? controlled_buffer_17_out[9] : 1'bz;  // Controlled_Buffer controlled_buffer_30
  assign controlled_buffer_18_out[10] = decoder_1_out3 ? controlled_buffer_17_out[10] : 1'bz;  // Controlled_Buffer controlled_buffer_31
  assign controlled_buffer_18_out[11] = decoder_1_out3 ? controlled_buffer_17_out[11] : 1'bz;  // Controlled_Buffer controlled_buffer_32
  assign controlled_buffer_18_out[15] = decoder_1_out3 ? in_7 : 1'bz;  // Controlled_Buffer controlled_buffer_33
  assign controlled_buffer_17_out = undriven_3 ? IR_q[15:4] : 12'bz;  // Controlled_Buffer controlled_buffer_34
  Register #(.trigger("falling"), .width(16)) IR (
    .D({{4{controlled_buffer_18_out[15]}}, controlled_buffer_18_out[11:0]}), .en(decoder_2_out11),
    .clk(MasterClock_out), .Q({IR_q, IR_q_2[9]}), .clr(button_1_out));
  Button button_1 (.out(button_1_out));
  LedBar #(.matrixcols(16)) ledbar_1 (
    .led0(IR_q_2[9]), .led1(IR_q[1]), .led2(IR_q[2]), .led3(IR_q[3]), .led4(IR_q[4]), .led5(IR_q[5]),
    .led6(IR_q[6]), .led7(IR_q[7]), .led8(IR_q[8]), .led9(IR_q[9]), .led10(IR_q[10]), .led11(IR_q[11]),
    .led12(IR_q[12]), .led13(IR_q[13]), .led14(IR_q[14]), .led15(IR_q[15]));
  assign and_1_out = rand_q & {{4{controlled_buffer_18_out[15]}}, controlled_buffer_18_out[11:0]};  // AND_Gate and_1, 16 bits wide
  Adder #(.width(16)) adder_1 (
    .a({DR_q_2[14:0], DR_q[0]}), .b({{4{controlled_buffer_18_out[15]}}, controlled_buffer_18_out[11:0]}),
    .out(adder_1_out), .cin(DR_q_2[15]), .cout(adder_1_cout));
  assign xor_1_out = rand_q ^ and_1_out;  // XOR_Gate xor_1, 16 bits wide
  Subtractor #(.width(16)) subtractor_1 (
    .a({DR_q_2[14:0], DR_q[0]}), .b({{4{controlled_buffer_18_out[15]}}, controlled_buffer_18_out[11:0]}),
    .out(subtractor_1_out), .bin(DR_q_2[15]), .bout(subtractor_1_bout));
  assign or_1_out = {{4{controlled_buffer_18_out[15]}}, controlled_buffer_18_out[11:0]} | {DR_q_2[14:0], DR_q[0]};  // OR_Gate or_1, 16 bits wide
  TTY tty_1 (.data(register_9_q_2), .clk(MasterClock_out), .we(decoder_2_out12), .clr(button_2_out));
  or or_2 (or_2_out, adder_1_cout, subtractor_1_bout);
  assign not_1_out = ~{DR_q_2[14:0], DR_q[0]};  // NOT_Gate not_1, 16 bits wide
  Register #(.width(16)) \rand  (.D(xor_1_out), .en(in_8), .clk(MasterClock_out), .Q(rand_q), .clr(button_1_out));
  or or_3 (or_3_out, DR_q[0], adder_2_cout);
  assign xor_2_out = {{4{controlled_buffer_18_out[15]}}, controlled_buffer_18_out[11:0]} ^ {DR_q_2[14:0], DR_q[0]};  // XOR_Gate xor_2, 16 bits wide
  or or_4 (or_4_out, or_2_out, or_3_out);
  assign and_2_out = {{4{controlled_buffer_18_out[15]}}, controlled_buffer_18_out[11:0]} & {DR_q_2[14:0], DR_q[0]};  // AND_Gate and_2, 16 bits wide
  assign and_3_out = {DR_q_2[14:0], DR_q[0]} & {16{undriven_4[15]}};  // AND_Gate and_3, 16 bits wide
  Adder #(.width(16)) adder_2 (.a(mAC_p1), .b(and_3_out), .out(adder_2_out), .cin(in_6), .cout(adder_2_cout));
  Button button_2 (.out(button_2_out));
  // Shift_Register #(.length(16)) mAC: pin names not known; wires that end beside it: mAC_p1, mAC_p2, CWR_q_2[14], CWR_q_2[15], MasterClock_out, in_6
  Register #(.width(16)) register_9 (
    .D({{4{controlled_buffer_18_out[15]}}, controlled_buffer_18_out[11:0]}), .en(decoder_2_out12),
    .clk(MasterClock_out), .Q({register_9_q, register_9_q_2}), .clr(button_1_out));
  Adder #(.width(16)) adder_3 (
    .a(in_3), .b({{4{controlled_buffer_18_out[15]}}, controlled_buffer_18_out[11:0]}), .out(adder_3_out));  // open: cin, cout
  Hex_Digit_Display #(.decimalPoint("false")) hex_digit_display_1 (.value(register_9_q[15:12]));
  Hex_Digit_Display #(.decimalPoint("false")) hex_digit_display_2 (.value(register_9_q[11:8]));
  Counter #(.max('h3ff), .width(10)) counter_1 (
    .clr(button_1_out), .up(undriven_5), .count(undriven_6), .clk(MasterClock_out),
    .D({IR_q_2[9], {9{in_1}}}), .Q(counter_1_q));  // open: load, carry
  Comparator #(.width(16)) comparator_1 (
    .a({{4{controlled_buffer_18_out[15]}}, controlled_buffer_18_out[11:0]}), .b({DR_q_2[14:0], DR_q[0]}),
    .gt(comparator_1_gt), .eq(comparator_1_eq), .lt(comparator_1_lt));
  Subtractor #(.width(16)) subtractor_2 (
    .a(dAC_p18), .b({DR_q_2[14:0], DR_q[0]}), .out(subtractor_2_out));  // open: bin, bout
  Hex_Digit_Display #(.decimalPoint("false")) hex_digit_display_3 (.value({register_9_q[7], register_9_q_2[6:4]}));
  or or_5 (mAC_p2, CWR_q_2[19], button_1_out);
  Multiplexer #(.width(16)) multiplexer_2 (
    .in0(subtractor_2_out), .in1({{4{controlled_buffer_18_out[15]}}, controlled_buffer_18_out[11:0]}),
    .out(multiplexer_2_out), .sel(and_4_out));
  assign {{4{controlled_buffer_18_out[15]}}, controlled_buffer_18_out[11:0]} = decoder_1_out10 ? dAC_p18 : 16'bz;  // Controlled_Buffer controlled_buffer_35
  Hex_Digit_Display #(.decimalPoint("false")) hex_digit_display_4 (.value(register_9_q_2[3:0]));
  and and_4 (and_4_out, and_5_out, CWR_q_2[14]);
  // Shift_Register #(.length(16)) dAC: pin names not known; wires that end beside it: mAC_p2, CWR_q_2[14], CWR_q_2[15], MasterClock_out, undriven_7[15], multiplexer_2_out[0], multiplexer_2_out[1], multiplexer_2_out[2], multiplexer_2_out[3], multiplexer_2_out[4], multiplexer_2_out[5], multiplexer_2_out[6], multiplexer_2_out[7], multiplexer_2_out[8], multiplexer_2_out[9], multiplexer_2_out[10], multiplexer_2_out[11], dAC_p18[0], dAC_p18[1], dAC_p18[2], dAC_p18[3], dAC_p18[4], dAC_p18[5], dAC_p18[6], dAC_p18[7], dAC_p18[8], dAC_p18[9], dAC_p18[10], dAC_p18[11]
  ROM #(.addrWidth(10), .dataWidth(32)) CNTRL_MEM (.addr({IR_q_2[9], {9{in_1}}}), .data(CNTRL_MEM_data));
  and and_5 (and_5_out, CWR_q_2[20], undriven_7[15]);
  not not_2 (not_2_out[0], dAC_p18[15]);
  Multiplexer #(.width(16)) multiplexer_3 (
    .in0({undriven_7[15:1], not_2_out[0]}),
    .in1({{4{controlled_buffer_18_out[15]}}, controlled_buffer_18_out[11:0]}), .out(multiplexer_3_out),
    .sel(decoder_2_out14));
  Register #(.trigger("falling"), .width(32)) CWR (
    .D(CNTRL_MEM_data), .en(1'b1), .clk(MasterClock_out), .Q({CWR_q_2[31:12], CWR_q, CWR_q_2[7:0]}),
    .clr(button_1_out));
  Multiplexer #(.enable("true"), .select(4), .width(16)) multiplexer_4 (
    .in0({DR_q_2[14:0], DR_q[0]}), .in1(not_1_out), .in2(adder_1_out), .in3(subtractor_1_out),
    .in4(or_1_out), .in5(xor_2_out), .in6(and_2_out), .in7(DR_q_2), .in8(in_2), .in9(rand_q),
    .in10(adder_3_out), .in11(mAC_p1), .in12(dAC_p18), .in13(in_2), .in14(in_2), .in15(in_2),
    .out(multiplexer_4_out), .sel(CWR_q), .en(CWR_q_2[12]));
  // Shift_Register #(.length(16)) Q: pin names not known; wires that end beside it: button_1_out, CWR_q_2[20], CWR_q_2[15], MasterClock_out, in_5, multiplexer_3_out[0], multiplexer_3_out[1], multiplexer_3_out[2], multiplexer_3_out[3], multiplexer_3_out[4], multiplexer_3_out[5], multiplexer_3_out[6], multiplexer_3_out[7], multiplexer_3_out[8], multiplexer_3_out[9], multiplexer_3_out[10], multiplexer_3_out[11]
  DotMatrix #(.matrixcols(32), .matrixrows(1)) dotmatrix_2 (
    .col0(CWR_q_2[0]), .col1(CWR_q_2[1]), .col2(CWR_q_2[2]), .col3(CWR_q_2[3]), .col4(CWR_q_2[4]),
    .col5(CWR_q_2[5]), .col6(CWR_q_2[6]), .col7(CWR_q_2[7]), .col8(CWR_q[0]), .col9(CWR_q[1]),
    .col10(CWR_q[2]), .col11(CWR_q[3]), .col12(CWR_q_2[12]), .col13(CWR_q_2[13]), .col14(CWR_q_2[14]),
    .col15(CWR_q_2[15]), .col16(CWR_q_2[16]), .col17(CWR_q_2[17]), .col18(CWR_q_2[18]), .col19(CWR_q_2[19]),
    .col20(CWR_q_2[20]), .col21(CWR_q_2[21]), .col22(CWR_q_2[22]), .col23(CWR_q_2[23]), .col24(CWR_q_2[24]),
    .col25(CWR_q_2[25]), .col26(CWR_q_2[26]), .col27(CWR_q_2[27]), .col28(CWR_q_2[28]), .col29(CWR_q_2[29]),
    .col30(CWR_q_2[30]), .col31(CWR_q_2[31]));
  // Probe on multiplexer_4_out
  assign {{4{controlled_buffer_18_out[15]}}, controlled_buffer_18_out[11:0]} = decoder_1_out11 ? undriven_7 : 16'bz;  // Controlled_Buffer controlled_buffer_36
  not not_3 (not_3_out, CWR_q[2]);
  nand nand_1 (nand_1_out, CWR_q[1], CWR_q[0]);
  and and_6 (and_6_out, not_3_out, nand_1_out);
  and and_7 (and_7_out, CWR_q[3], and_6_out);
  buf buffer_1 (CWR_q_2[18], or_4_out);
  Multiplexer #(.select(2)) multiplexer_5 (
    .in0(carry_q), .in1(comparator_1_lt), .in2(comparator_1_eq), .in3(comparator_1_gt),
    .out(multiplexer_5_out), .sel(CWR_q_2[17:16]));
  // Shift_Register #(.length(16)) AC: pin names not known; wires that end beside it: button_1_out, AC_p2, AC_p3, MasterClock_out, DR_q_2[15], multiplexer_4_out[0], multiplexer_4_out[1], multiplexer_4_out[2], multiplexer_4_out[3], multiplexer_4_out[4], multiplexer_4_out[5], multiplexer_4_out[6], multiplexer_4_out[7], multiplexer_4_out[8], multiplexer_4_out[9], multiplexer_4_out[10], multiplexer_4_out[11], AC_p18, AC_p19, AC_p20, AC_p21, AC_p22, AC_p23, AC_p24, AC_p25, AC_p26, AC_p27, AC_p28
  RAM #(.addrWidth(12), .dataWidth(16), .databus("bidir"), .enables("line")) MEM (
    .addr(controlled_buffer_17_out), .we(decoder_2_out1), .oe(decoder_1_out1), .clk(MasterClock_out),
    .data({{4{controlled_buffer_18_out[15]}}, controlled_buffer_18_out[11:0]}));
  Decoder #(.enable("false"), .select(4)) decoder_1 (
    .out0(decoder_1_out0), .out1(decoder_1_out1), .out2(decoder_1_out2), .out3(decoder_1_out3),
    .out5(decoder_1_out5), .out10(decoder_1_out10), .out11(decoder_1_out11), .out12(decoder_1_out12),
    .out13(decoder_1_out13), .sel(CWR_q_2[3:0]));  // open: out4, out6, out7, out8, out9, out14, out15
  Decoder #(.enable("false"), .select(4)) decoder_2 (
    .out0(decoder_2_out0), .out1(decoder_2_out1), .out2(AC_p2), .out3(decoder_2_out3), .out5(decoder_2_out5),
    .out10(decoder_2_out10), .out11(decoder_2_out11), .out12(decoder_2_out12), .out13(decoder_2_out13),
    .out14(decoder_2_out14), .out15(decoder_2_out15), .sel(CWR_q_2[7:4]));  // open: out4, out6, out7, out8, out9
  D_Flip_Flop carry (.D(or_4_out), .clk(MasterClock_out), .Q(carry_q), .reset(button_1_out));  // open: Qn, preset
  or or_6 (or_6_out, or_4_out, multiplexer_5_out);
  Controlled_Buffer controlled_buffer_37 (.out(controlled_buffer_18_out[0]), .en(decoder_1_out2));  // open: in
  assign controlled_buffer_18_out[1] = decoder_1_out2 ? AC_p18 : 1'bz;  // Controlled_Buffer controlled_buffer_38
  assign controlled_buffer_18_out[2] = decoder_1_out2 ? AC_p19 : 1'bz;  // Controlled_Buffer controlled_buffer_39
  assign controlled_buffer_18_out[3] = decoder_1_out2 ? AC_p20 : 1'bz;  // Controlled_Buffer controlled_buffer_40
  assign controlled_buffer_18_out[4] = decoder_1_out2 ? AC_p21 : 1'bz;  // Controlled_Buffer controlled_buffer_41
  assign controlled_buffer_18_out[5] = decoder_1_out2 ? AC_p22 : 1'bz;  // Controlled_Buffer controlled_buffer_42
  assign controlled_buffer_18_out[6] = decoder_1_out2 ? AC_p23 : 1'bz;  // Controlled_Buffer controlled_buffer_43
  assign controlled_buffer_18_out[7] = decoder_1_out2 ? AC_p24 : 1'bz;  // Controlled_Buffer controlled_buffer_44
  assign controlled_buffer_18_out[8] = decoder_1_out2 ? AC_p25 : 1'bz;  // Controlled_Buffer controlled_buffer_45
  assign controlled_buffer_18_out[9] = decoder_1_out2 ? AC_p26 : 1'bz;  // Controlled_Buffer controlled_buffer_46
  assign controlled_buffer_18_out[10] = decoder_1_out2 ? AC_p27 : 1'bz;  // Controlled_Buffer controlled_buffer_47
  assign controlled_buffer_18_out[11] = decoder_1_out2 ? AC_p28 : 1'bz;  // Controlled_Buffer controlled_buffer_48
  assign controlled_buffer_18_out[15] = decoder_1_out2 ? undriven_8 : 1'bz;  // Controlled_Buffer controlled_buffer_49
  assign controlled_buffer_18_out[15] = decoder_1_out2 ? undriven_9 : 1'bz;  // Controlled_Buffer controlled_buffer_50
  assign controlled_buffer_18_out[15] = decoder_1_out2 ? undriven_10 : 1'bz;  // Controlled_Buffer controlled_buffer_51
  assign controlled_buffer_18_out[15] = decoder_1_out2 ? undriven_4[15] : 1'bz;  // Controlled_Buffer controlled_buffer_52
  LED led_4 (.in(decoder_1_out0));
  LED led_5 (.in(decoder_2_out0));
  Register #(.width(1)) register_10 (
    .D(or_6_out), .en(in_4), .clk(MasterClock_out), .Q(register_10_q), .clr(button_1_out));
  D_Flip_Flop d_ff_1 (
    .D(decoder_2_out13), .clk(MasterClock_out), .Q(DR_q_2[15]), .reset(button_1_out));  // open: Qn, preset
  or or_7 (AC_p3, and_7_out, CWR_q_2[13]);

  // Notes on the sheet:
  //   CLOCK
  //   16 LINES
  //   STACK OVERFLOW
  //   STACK
  //   ADDRESS BUS
  //   END OF THE LINE
  //   PRESENT BUS VALUES
  //   COMPUTER RESET
  //   ADDRESS BUS
  //   PRESENT INSTRUCTION
  //   NXT INSN FRM MEM OR CNTRL MEM
  //   CONDITION
  //   AC RESET ASYNC
  //   ADDRESSING MODE
  //   OP-CODE
  //   GENERAL SYSTEM BUS
  //   ADDRESS BUS
  //   CONTROL UNIT
  //   ALU
  //   LEAST SIGNIFICANT LINE
  //   ADDRESS BUS
  //   MOST SIGNIFICANT LINE
  //   OUTPUT
  //   ADDRESS BUS
  //   this line is just a place holder
  //   PRESENT CONTROL
  //   STACK POINTER VALUE MANIPULATE
  //   ADDRESS BUS
  //   ACC SHIFT(L)
  //   NONE
  //   MEM OUT ENABLE
  //   ACC ON BUS
  //   PC ON BUS
  //   AR ON BUS
  //   dAC ON BUS
  //   Q ON BUS
  //   STACK TOP ON BUS
  //   IR ON BUS(GENERAL)
  //   NONE
  //   MEM WRITE ENABLE
  //   AC PARLLEL LOAD
  //   PC LOAD
  //   PC LOAD
  //   AR LOAD
  //   DR LOAD
  //   IR LOAD
  //   OUT LOAD
  //   SRL IN
  //   LOAD Q
  //   PUSH TO STACK
  //   CONDITION FLIP FLOP
  //   PUT ON BUS
  //   SERIAL IN
  //   LOAD FROM BUS
endmodule
